// Logisim project relogio.circ as structural Verilog: 11 circuits, main circuit main
module main (
  input  in_1
);

  wire clock_1_out, contador_completo_1_out_4, contador_completo_1_out_5, contador_completo_1_out_6,
       contador_completo_1_out_7, contador_completo_1_out_8, contador_completo_1_out_9,
       contador_completo_1_out_10, contador_completo_1_out_11, contador_completo_1_out_12,
       contador_completo_1_out_13, contador_completo_1_out_14, contador_completo_1_out_15,
       contador_completo_1_out_16, contador_completo_1_out_17, contador_completo_1_out_18,
       contador_completo_1_out_19, contador_completo_1_out_20, contador_completo_1_out_21,
       contador_completo_1_out_22, contador_completo_1_out_23, contador_completo_1_out_24,
       contador_completo_1_out_25, contador_completo_1_out_26, contador_completo_1_out_27,
       contador_completo_1_out_28, decodificador4bin_0_9dec_1_a_2, decodificador4bin_0_9dec_1_b_2,
       decodificador4bin_0_9dec_1_c_2, decodificador4bin_0_9dec_1_d_2, decodificador4bin_0_9dec_1_e,
       decodificador4bin_0_9dec_1_f, decodificador4bin_0_9dec_1_x, decodificador4bin_0_9dec_2_a_2,
       decodificador4bin_0_9dec_2_b_2, decodificador4bin_0_9dec_2_c_2, decodificador4bin_0_9dec_2_d_2,
       decodificador4bin_0_9dec_2_e, decodificador4bin_0_9dec_2_f, decodificador4bin_0_9dec_2_x,
       decodificador4bin_0_9dec_3_a_2, decodificador4bin_0_9dec_3_b_2, decodificador4bin_0_9dec_3_c_2,
       decodificador4bin_0_9dec_3_d_2, decodificador4bin_0_9dec_3_e, decodificador4bin_0_9dec_3_f,
       decodificador4bin_0_9dec_3_x, decodificador4bin_0_9dec_4_a_2, decodificador4bin_0_9dec_4_b_2,
       decodificador4bin_0_9dec_4_c_2, decodificador4bin_0_9dec_4_d_2, decodificador4bin_0_9dec_4_e,
       decodificador4bin_0_9dec_4_f, decodificador4bin_0_9dec_4_x, mux_1_out_10, mux_1_out_11, mux_1_out_12,
       mux_1_out_13, mux_2_out_10, mux_2_out_11, mux_2_out_12, mux_2_out_13, mux_3_out_10, mux_3_out_11,
       mux_3_out_12, mux_3_out_13, mux_4_out_10, mux_4_out_11, mux_4_out_12, mux_4_out_13;

  Clock clock_1 (.out(clock_1_out));
  _7_Segment_Display u_7_segment_display_1 (
    .g(decodificador4bin_0_9dec_1_x), .f(decodificador4bin_0_9dec_1_f), .a(decodificador4bin_0_9dec_1_a_2),
    .b(decodificador4bin_0_9dec_1_b_2), .e(decodificador4bin_0_9dec_1_e), .d(decodificador4bin_0_9dec_1_d_2),
    .c(decodificador4bin_0_9dec_1_c_2));  // open: dp
  decodificador4bin_0_9dec decodificador4bin_0_9dec_1 (
    .D(mux_1_out_10), .C(mux_1_out_11), .B(mux_1_out_12), .A(mux_1_out_13),
    .a_2(decodificador4bin_0_9dec_1_a_2), .b_2(decodificador4bin_0_9dec_1_b_2),
    .c_2(decodificador4bin_0_9dec_1_c_2), .d_2(decodificador4bin_0_9dec_1_d_2),
    .e(decodificador4bin_0_9dec_1_e), .f(decodificador4bin_0_9dec_1_f), .x(decodificador4bin_0_9dec_1_x));
  mux mux_1 (
    .a(contador_completo_1_out_6), .b(contador_completo_1_out_7), .c(contador_completo_1_out_8),
    .d(contador_completo_1_out_9), .A_2(contador_completo_1_out_14), .B_2(contador_completo_1_out_15),
    .C_2(contador_completo_1_out_16), .D_2(contador_completo_1_out_17), .SELECT(contador_completo_1_out_4),
    .out_10(mux_1_out_10), .out_11(mux_1_out_11), .out_12(mux_1_out_12), .out_13(mux_1_out_13));
  _7_Segment_Display u_7_segment_display_2 (
    .g(decodificador4bin_0_9dec_2_x), .f(decodificador4bin_0_9dec_2_f), .a(decodificador4bin_0_9dec_2_a_2),
    .b(decodificador4bin_0_9dec_2_b_2), .e(decodificador4bin_0_9dec_2_e), .d(decodificador4bin_0_9dec_2_d_2),
    .c(decodificador4bin_0_9dec_2_c_2));  // open: dp
  decodificador4bin_0_9dec decodificador4bin_0_9dec_2 (
    .D(mux_2_out_10), .C(mux_2_out_11), .B(mux_2_out_12), .A(mux_2_out_13),
    .a_2(decodificador4bin_0_9dec_2_a_2), .b_2(decodificador4bin_0_9dec_2_b_2),
    .c_2(decodificador4bin_0_9dec_2_c_2), .d_2(decodificador4bin_0_9dec_2_d_2),
    .e(decodificador4bin_0_9dec_2_e), .f(decodificador4bin_0_9dec_2_f), .x(decodificador4bin_0_9dec_2_x));
  mux mux_2 (
    .a(contador_completo_1_out_10), .b(contador_completo_1_out_11), .c(contador_completo_1_out_12),
    .d(contador_completo_1_out_13), .A_2(contador_completo_1_out_18), .B_2(contador_completo_1_out_19),
    .C_2(contador_completo_1_out_20), .D_2(contador_completo_1_out_21), .SELECT(contador_completo_1_out_4),
    .out_10(mux_2_out_10), .out_11(mux_2_out_11), .out_12(mux_2_out_12), .out_13(mux_2_out_13));
  contador_completo contador_completo_1 (
    .PRESET(in_1), .clock(clock_1_out), .VCC(1'b1), .out_6(contador_completo_1_out_6),
    .out_7(contador_completo_1_out_7), .out_8(contador_completo_1_out_8), .out_9(contador_completo_1_out_9),
    .out_10(contador_completo_1_out_10), .out_11(contador_completo_1_out_11),
    .out_12(contador_completo_1_out_12), .out_13(contador_completo_1_out_13),
    .out_14(contador_completo_1_out_14), .out_15(contador_completo_1_out_15),
    .out_16(contador_completo_1_out_16), .out_17(contador_completo_1_out_17),
    .out_18(contador_completo_1_out_18), .out_19(contador_completo_1_out_19),
    .out_20(contador_completo_1_out_20), .out_21(contador_completo_1_out_21),
    .out_22(contador_completo_1_out_22), .out_5(contador_completo_1_out_5),
    .out_23(contador_completo_1_out_23), .out_24(contador_completo_1_out_24),
    .out_25(contador_completo_1_out_25), .out_26(contador_completo_1_out_26),
    .out_27(contador_completo_1_out_27), .out_28(contador_completo_1_out_28),
    .out_4(contador_completo_1_out_4));
  decodificador4bin_0_9dec decodificador4bin_0_9dec_3 (
    .D(mux_3_out_10), .C(mux_3_out_11), .B(mux_3_out_12), .A(mux_3_out_13),
    .a_2(decodificador4bin_0_9dec_3_a_2), .b_2(decodificador4bin_0_9dec_3_b_2),
    .c_2(decodificador4bin_0_9dec_3_c_2), .d_2(decodificador4bin_0_9dec_3_d_2),
    .e(decodificador4bin_0_9dec_3_e), .f(decodificador4bin_0_9dec_3_f), .x(decodificador4bin_0_9dec_3_x));
  _7_Segment_Display u_7_segment_display_3 (
    .g(decodificador4bin_0_9dec_3_x), .f(decodificador4bin_0_9dec_3_f), .a(decodificador4bin_0_9dec_3_a_2),
    .b(decodificador4bin_0_9dec_3_b_2), .e(decodificador4bin_0_9dec_3_e), .d(decodificador4bin_0_9dec_3_d_2),
    .c(decodificador4bin_0_9dec_3_c_2));  // open: dp
  mux mux_3 (
    .a(contador_completo_1_out_14), .b(contador_completo_1_out_15), .c(contador_completo_1_out_16),
    .d(contador_completo_1_out_17), .A_2(contador_completo_1_out_22), .B_2(contador_completo_1_out_5),
    .C_2(contador_completo_1_out_23), .D_2(contador_completo_1_out_24), .SELECT(contador_completo_1_out_4),
    .out_10(mux_3_out_10), .out_11(mux_3_out_11), .out_12(mux_3_out_12), .out_13(mux_3_out_13));
  _7_Segment_Display u_7_segment_display_4 (
    .g(decodificador4bin_0_9dec_4_x), .f(decodificador4bin_0_9dec_4_f), .a(decodificador4bin_0_9dec_4_a_2),
    .b(decodificador4bin_0_9dec_4_b_2), .e(decodificador4bin_0_9dec_4_e), .d(decodificador4bin_0_9dec_4_d_2),
    .c(decodificador4bin_0_9dec_4_c_2));  // open: dp
  decodificador4bin_0_9dec decodificador4bin_0_9dec_4 (
    .D(mux_4_out_10), .C(mux_4_out_11), .B(mux_4_out_12), .A(mux_4_out_13),
    .a_2(decodificador4bin_0_9dec_4_a_2), .b_2(decodificador4bin_0_9dec_4_b_2),
    .c_2(decodificador4bin_0_9dec_4_c_2), .d_2(decodificador4bin_0_9dec_4_d_2),
    .e(decodificador4bin_0_9dec_4_e), .f(decodificador4bin_0_9dec_4_f), .x(decodificador4bin_0_9dec_4_x));
  mux mux_4 (
    .a(contador_completo_1_out_18), .b(contador_completo_1_out_19), .c(contador_completo_1_out_20),
    .d(contador_completo_1_out_21), .A_2(contador_completo_1_out_25), .B_2(contador_completo_1_out_26),
    .C_2(contador_completo_1_out_27), .D_2(contador_completo_1_out_28), .SELECT(contador_completo_1_out_4),
    .out_10(mux_4_out_10), .out_11(mux_4_out_11), .out_12(mux_4_out_12), .out_13(mux_4_out_13));
endmodule

module contador4bits (
  input  PRESET,
  input  CLK,
  input  VCC,
  output out_4,
  output out_5,
  output out_6,
  output out_7,
  output out_8
);

  wire fliflopjk_1_out_7, fliflopjk_2_out_7, fliflopjk_3_out_7;

  and and_1 (out_8, out_7, fliflopjk_3_out_7, out_5, fliflopjk_1_out_7);
  fliflopjk fliflopjk_1 (
    .PRESET(PRESET), .J(VCC), .CLK(CLK), .K(VCC), .CLEAR(out_8), .out_6(out_4), .out_7(fliflopjk_1_out_7));
  fliflopjk fliflopjk_2 (
    .PRESET(PRESET), .J(VCC), .CLK(fliflopjk_1_out_7), .K(VCC), .CLEAR(out_8), .out_6(out_5),
    .out_7(fliflopjk_2_out_7));
  fliflopjk fliflopjk_3 (
    .PRESET(PRESET), .J(VCC), .CLK(fliflopjk_2_out_7), .K(VCC), .CLEAR(out_8), .out_6(out_6),
    .out_7(fliflopjk_3_out_7));
  fliflopjk fliflopjk_4 (
    .PRESET(PRESET), .J(VCC), .CLK(fliflopjk_3_out_7), .K(VCC), .CLEAR(out_8), .out_6(out_7));  // open: out_7

  // Notes on the sheet:
  //   CLK: pull=up
  //   out_7: pull=up
  //   VCC: pull=up
  //   out_6: pull=up
  //   PRESET: pull=up
  //   out_8: pull=up
  //   out_4: pull=up
  //   out_5: pull=up
endmodule

module fliflopjk (
  input  PRESET,
  input  J,
  input  CLK,
  input  K,
  input  CLEAR,
  output out_6,
  output out_7
);

  wire nand_1_out, nand_2_out, nand_3_out, nand_4_out, nand_5_out, nand_6_out, not_1_out, not_2_out,
       not_3_out, or_1_out;

  or or_1 (or_1_out, PRESET, CLEAR);
  not not_1 (not_1_out, or_1_out);
  not not_2 (not_2_out, CLK);
  nand nand_1 (nand_1_out, out_7, J, not_2_out);
  nand nand_2 (nand_2_out, not_2_out, K, out_6);
  nand nand_3 (nand_3_out, 1'b1, nand_1_out, nand_4_out);
  nand nand_4 (nand_4_out, nand_3_out, nand_2_out, not_1_out);
  nand nand_5 (nand_5_out, not_1_out, nand_3_out, not_3_out);
  not not_3 (not_3_out, not_2_out);
  nand nand_6 (nand_6_out, not_3_out, nand_4_out, 1'b1);
  nand nand_7 (out_6, 1'b1, nand_5_out, out_7);
  nand nand_8 (out_7, out_6, nand_6_out, not_1_out);

  // Notes on the sheet:
  //   CLEAR: pull=up
  //   K: pull=up
  //   out_6: pull=up
  //   J: pull=up
  //   CLK: pull=up
  //   out_7: pull=up
endmodule

module contador_completo (
  input  PRESET,
  input  clock,
  input  VCC,
  output out_4,
  output out_5,
  output out_6,
  output out_7,
  output out_8,
  output out_9,
  output out_10,
  output out_11,
  output out_12,
  output out_13,
  output out_14,
  output out_15,
  output out_16,
  output out_17,
  output out_18,
  output out_19,
  output out_20,
  output out_21,
  output out_22,
  output out_23,
  output out_24,
  output out_25,
  output out_26,
  output out_27,
  output out_28
);

  wire and_1_out, contador4bits6_1_out_8, contador4bits6_2_out_8, contador4bits_1_out_8,
       contador4bits_2_out_8, count15_1_out_4, count15_1_out_5, count15_1_out_6, count15_1_out_7,
       counthourdec_1_soutforcount, hourcont_1_sout;

  contador4bits contador4bits_1 (
    .out_8(contador4bits_1_out_8), .out_4(out_6), .out_5(out_7), .out_6(out_8), .out_7(out_9),
    .PRESET(PRESET), .VCC(VCC), .CLK(clock));
  contador4bits6 contador4bits6_1 (
    .PRESET(PRESET), .CLK(contador4bits_1_out_8), .VCC(VCC), .out_4(out_10), .out_5(out_11), .out_6(out_12),
    .out_7(out_13), .out_8(contador4bits6_1_out_8));
  contador4bits contador4bits_2 (
    .out_8(contador4bits_2_out_8), .out_4(out_14), .out_5(out_15), .out_6(out_16), .out_7(out_17),
    .PRESET(PRESET), .VCC(VCC), .CLK(contador4bits6_1_out_8));
  contador4bits6 contador4bits6_2 (
    .PRESET(PRESET), .CLK(contador4bits_2_out_8), .VCC(VCC), .out_4(out_18), .out_5(out_19), .out_6(out_20),
    .out_7(out_21), .out_8(contador4bits6_2_out_8));
  hourCont hourcont_1 (
    .PRESET(PRESET), .CLK(contador4bits6_2_out_8), .VCC(VCC), .Sin(counthourdec_1_soutforcount), .q1(out_22),
    .q2(out_5), .q3(out_23), .q4(out_24), .Sout(hourcont_1_sout));
  countHourDec counthourdec_1 (
    .PRESET(PRESET), .CLK(hourcont_1_sout), .VCC(VCC), .q1(out_25), .q2(out_26), .q3(out_27), .q4(out_28),
    .soutForCount(counthourdec_1_soutforcount));
  and and_1 (and_1_out, count15_1_out_4, count15_1_out_5, count15_1_out_7, count15_1_out_6);
  count15 count15_1 (
    .PRESET(PRESET), .CLK(clock), .VCC(VCC), .out_4(count15_1_out_4), .out_5(count15_1_out_5),
    .out_6(count15_1_out_6), .out_7(count15_1_out_7));
  fliflopjk fliflopjk_1 (
    .PRESET(PRESET), .J(VCC), .CLK(and_1_out), .K(VCC), .CLEAR(PRESET), .out_6(out_4));  // open: out_7

  // Notes on the sheet:
  //   out_9: pull=up
  //   out_5: pull=up
  //   out_27: pull=up
  //   out_18: pull=up
  //   out_6: pull=up
  //   out_16: pull=up
  //   out_8: pull=up
  //   out_17: pull=up
  //   out_24: pull=up
  //   out_15: pull=up
  //   PRESET: pull=up
  //   out_23: pull=up
  //   out_28: pull=up
  //   out_4: pull=up
  //   out_26: pull=up
  //   out_22: pull=up
  //   out_19: pull=up
  //   out_14: pull=up
  //   out_7: pull=up
  //   out_12: pull=up
  //   out_13: pull=up
  //   out_20: pull=up
  //   out_25: pull=up
  //   out_21: pull=up
  //   out_10: pull=up
  //   VCC: pull=up
  //   out_11: pull=up
endmodule

module decodificador4bin_0_9dec (
  input  D,
  input  C,
  input  B,
  input  A,
  output a_2,
  output b_2,
  output c_2,
  output d_2,
  output e,
  output f,
  output x
);

  wire and_1_out, and_2_out, and_3_out, and_4_out, and_5_out, and_6_out, and_7_out, and_8_out, and_9_out,
       and_10_out, and_11_out, and_12_out, and_13_out, and_14_out, and_15_out, and_16_out, and_17_out,
       and_18_out, and_19_out, not_1_out, not_2_out, not_3_out, not_4_out, not_5_out, not_6_out, not_7_out,
       not_8_out, not_9_out, not_10_out, not_11_out, not_12_out, not_13_out, not_14_out, not_15_out,
       not_16_out, not_17_out, not_18_out, not_19_out, not_20_out, not_21_out;

  not not_1 (not_1_out, B);
  and and_1 (and_1_out, not_1_out, not_2_out);
  not not_2 (not_2_out, D);
  and and_2 (and_2_out, B, D);
  not not_3 (not_3_out, B);
  not not_4 (not_4_out, C);
  and and_3 (and_3_out, not_4_out, not_5_out);
  not not_5 (not_5_out, D);
  and and_4 (and_4_out, C, D);
  not not_6 (not_6_out, C);
  not not_7 (not_7_out, B);
  and and_5 (and_5_out, not_7_out, not_8_out);
  not not_8 (not_8_out, D);
  not not_9 (not_9_out, B);
  and and_6 (and_6_out, not_9_out, C);
  and and_7 (and_7_out, C, not_10_out);
  not not_10 (not_10_out, D);
  and and_8 (and_8_out, B, not_11_out, D);
  not not_11 (not_11_out, C);
  and and_9 (and_9_out, A, B);
  not not_12 (not_12_out, B);
  and and_10 (and_10_out, not_12_out, not_13_out);
  not not_13 (not_13_out, D);
  and and_11 (and_11_out, C, not_14_out);
  not not_14 (not_14_out, D);
  and and_12 (and_12_out, A, C);
  and and_13 (and_13_out, A, B);
  not not_15 (not_15_out, C);
  and and_14 (and_14_out, not_15_out, not_16_out);
  not not_16 (not_16_out, D);
  and and_15 (and_15_out, B, not_17_out);
  not not_17 (not_17_out, C);
  and and_16 (and_16_out, B, not_18_out);
  not not_18 (not_18_out, D);
  not not_19 (not_19_out, B);
  and and_17 (and_17_out, not_19_out, C);
  and and_18 (and_18_out, B, not_20_out);
  not not_20 (not_20_out, C);
  and and_19 (and_19_out, B, not_21_out);
  not not_21 (not_21_out, D);
  or or_1 (a_2, and_1_out, C, and_2_out, A);
  or or_2 (b_2, not_3_out, and_3_out, and_4_out, A);
  or or_3 (c_2, not_6_out, D, B, A);
  or or_4 (d_2, and_5_out, and_6_out, and_7_out, and_8_out, and_9_out);
  or or_5 (e, and_10_out, and_11_out, and_12_out, and_13_out);
  or or_6 (f, and_14_out, and_15_out, and_16_out, A);
  or or_7 (x, and_17_out, and_18_out, and_19_out, A);
endmodule

module contador4bits6 (
  input  PRESET,
  input  CLK,
  input  VCC,
  output out_4,
  output out_5,
  output out_6,
  output out_7,
  output out_8
);

  wire fliflopjk_1_out_7, fliflopjk_2_out_7, fliflopjk_3_out_7, fliflopjk_4_out_7;

  and and_1 (out_8, fliflopjk_4_out_7, out_6, fliflopjk_2_out_7, out_4);
  fliflopjk fliflopjk_1 (
    .PRESET(PRESET), .J(VCC), .CLK(CLK), .K(VCC), .CLEAR(out_8), .out_6(out_4), .out_7(fliflopjk_1_out_7));
  fliflopjk fliflopjk_2 (
    .PRESET(PRESET), .J(VCC), .CLK(fliflopjk_1_out_7), .K(VCC), .CLEAR(out_8), .out_6(out_5),
    .out_7(fliflopjk_2_out_7));
  fliflopjk fliflopjk_3 (
    .PRESET(PRESET), .J(VCC), .CLK(fliflopjk_2_out_7), .K(VCC), .CLEAR(out_8), .out_6(out_6),
    .out_7(fliflopjk_3_out_7));
  fliflopjk fliflopjk_4 (
    .PRESET(PRESET), .J(VCC), .CLK(fliflopjk_3_out_7), .K(VCC), .CLEAR(out_8), .out_6(out_7),
    .out_7(fliflopjk_4_out_7));

  // Notes on the sheet:
  //   VCC: pull=up
  //   CLK: pull=up
  //   out_5: pull=up
  //   PRESET: pull=up
  //   out_8: pull=up
  //   out_4: pull=up
  //   out_6: pull=up
  //   out_7: pull=up
endmodule

module hourCont (
  input  PRESET,
  input  CLK,
  input  VCC,
  input  Sin,
  output q1,
  output q2,
  output q3,
  output q4,
  output Sout
);

  wire and_1_out, and_2_out, fliflopjk_1_out_7, fliflopjk_2_out_7, fliflopjk_3_out_7, fliflopjk_4_out_7;

  and and_1 (and_1_out, q4, fliflopjk_3_out_7, q2, fliflopjk_1_out_7);
  fliflopjk fliflopjk_1 (
    .PRESET(PRESET), .J(VCC), .CLK(CLK), .K(VCC), .CLEAR(Sout), .out_6(q1), .out_7(fliflopjk_1_out_7));
  and and_2 (and_2_out, Sin, q2, q1, q2, fliflopjk_4_out_7);
  fliflopjk fliflopjk_2 (
    .PRESET(PRESET), .J(VCC), .CLK(fliflopjk_1_out_7), .K(VCC), .CLEAR(Sout), .out_6(q2),
    .out_7(fliflopjk_2_out_7));
  fliflopjk fliflopjk_3 (
    .PRESET(PRESET), .J(VCC), .CLK(fliflopjk_2_out_7), .K(VCC), .CLEAR(Sout), .out_6(q3),
    .out_7(fliflopjk_3_out_7));
  or or_1 (Sout, and_1_out, and_2_out);
  fliflopjk fliflopjk_4 (
    .PRESET(PRESET), .J(VCC), .CLK(fliflopjk_3_out_7), .K(VCC), .CLEAR(Sout), .out_6(q4),
    .out_7(fliflopjk_4_out_7));

  // Notes on the sheet:
  //   q2: pull=up
  //   Sout: pull=up
  //   q1: pull=up
  //   q4: pull=up
  //   q3: pull=up
  //   CLK: pull=up
  //   VCC: pull=up
  //   PRESET: pull=up
endmodule

module countHourDec (
  input  PRESET,
  input  CLK,
  input  VCC,
  output q1,
  output q2,
  output q3,
  output q4,
  output soutForCount
);

  wire and_1_out, fliflopjk_1_out_7, fliflopjk_2_out_7, fliflopjk_3_out_7, fliflopjk_4_out_7;

  and and_1 (and_1_out, fliflopjk_1_out_7, q2, fliflopjk_4_out_7, fliflopjk_3_out_7);
  and and_2 (soutForCount, q1, fliflopjk_2_out_7, fliflopjk_3_out_7, fliflopjk_4_out_7);
  fliflopjk fliflopjk_1 (
    .PRESET(PRESET), .J(VCC), .CLK(CLK), .K(VCC), .CLEAR(and_1_out), .out_6(q1), .out_7(fliflopjk_1_out_7));
  fliflopjk fliflopjk_2 (
    .PRESET(PRESET), .J(VCC), .CLK(fliflopjk_1_out_7), .K(VCC), .CLEAR(and_1_out), .out_6(q2),
    .out_7(fliflopjk_2_out_7));
  fliflopjk fliflopjk_3 (
    .PRESET(PRESET), .J(VCC), .CLK(fliflopjk_2_out_7), .K(VCC), .CLEAR(and_1_out), .out_6(q3),
    .out_7(fliflopjk_3_out_7));
  fliflopjk fliflopjk_4 (
    .PRESET(PRESET), .J(VCC), .CLK(fliflopjk_3_out_7), .K(VCC), .CLEAR(and_1_out), .out_6(q4),
    .out_7(fliflopjk_4_out_7));

  // Notes on the sheet:
  //   q1: pull=up
  //   soutForCount: pull=up
  //   q3: pull=up
  //   VCC: pull=up
  //   CLK: pull=up
  //   PRESET: pull=up
  //   q4: pull=up
  //   q2: pull=up
endmodule

module mux (
  input  a,
  input  b,
  input  c,
  input  d,
  input  A_2,
  input  B_2,
  input  C_2,
  input  D_2,
  input  SELECT,
  output out_10,
  output out_11,
  output out_12,
  output out_13
);

  wire and_1_out, and_2_out, and_3_out, and_4_out, and_5_out, and_6_out, and_7_out, and_8_out, not_1_out,
       not_2_out, not_3_out, not_4_out;

  and and_1 (and_1_out, a, not_1_out);
  not not_1 (not_1_out, SELECT);
  and and_2 (and_2_out, b, not_2_out);
  not not_2 (not_2_out, SELECT);
  and and_3 (and_3_out, c, not_3_out);
  not not_3 (not_3_out, SELECT);
  and and_4 (and_4_out, d, not_4_out);
  not not_4 (not_4_out, SELECT);
  and and_5 (and_5_out, A_2, SELECT);
  and and_6 (and_6_out, B_2, SELECT);
  and and_7 (and_7_out, C_2, SELECT);
  and and_8 (and_8_out, D_2, SELECT);
  or or_1 (out_10, and_1_out, and_5_out);
  or or_2 (out_11, and_2_out, and_6_out);
  or or_3 (out_12, and_3_out, and_7_out);
  or or_4 (out_13, and_4_out, and_8_out);
endmodule

module change_clock (
  input  in_1,
  input  in_2,
  input  in_3,
  input  in_4
);
endmodule

module count15 (
  input  PRESET,
  input  CLK,
  input  VCC,
  output out_4,
  output out_5,
  output out_6,
  output out_7
);

  wire fliflopjk_1_out_7, fliflopjk_2_out_7, fliflopjk_3_out_7;

  fliflopjk fliflopjk_1 (
    .PRESET(PRESET), .J(VCC), .CLK(CLK), .K(VCC), .CLEAR(PRESET), .out_6(out_4), .out_7(fliflopjk_1_out_7));
  fliflopjk fliflopjk_2 (
    .PRESET(PRESET), .J(VCC), .CLK(fliflopjk_1_out_7), .K(VCC), .CLEAR(PRESET), .out_6(out_5),
    .out_7(fliflopjk_2_out_7));
  fliflopjk fliflopjk_3 (
    .PRESET(PRESET), .J(VCC), .CLK(fliflopjk_2_out_7), .K(VCC), .CLEAR(PRESET), .out_6(out_6),
    .out_7(fliflopjk_3_out_7));
  fliflopjk fliflopjk_4 (
    .PRESET(PRESET), .J(VCC), .CLK(fliflopjk_3_out_7), .K(VCC), .CLEAR(PRESET), .out_6(out_7));  // open: out_7

  // Notes on the sheet:
  //   out_4: pull=up
  //   CLK: pull=up
  //   out_6: pull=up
  //   out_7: pull=up
  //   out_5: pull=up
  //   PRESET: pull=up
  //   VCC: pull=up
endmodule
